// Logisim project ALSU_18BCE259.circ as structural Verilog: 4 circuits, main circuit main
module main (
  input  [4:0] Selection_Bits,
  input  Cin,
  input  [7:0] A,
  input  [7:0] B,
  input  Select_A_or_B,
  input  Serial_Input,
  output Cout,
  output [7:0] Answer,
  output OverFlow
);

  wire [7:0] Arithmetic_Unit_answer, Logical_Unit_out_4, multiplexer_1_out, Shift_Unit_answer;

  Multiplexer #(.width(8)) multiplexer_1 (.in0(A), .in1(B), .out(multiplexer_1_out), .sel(Select_A_or_B));  // open: en
  Arithmetic_Unit Arithmetic_Unit (
    .Cin(Cin), .A(A), .B(B), .Selection(Selection_Bits[3:2]), .Answer(Arithmetic_Unit_answer), .Cout(Cout));
  Logical_Unit Logical_Unit (.Selection(Selection_Bits[3:2]), .A(A), .B(B), .out_4(Logical_Unit_out_4));
  Shift_Unit Shift_Unit (
    .Selection(Selection_Bits[4:2]), .Serial_Input(Serial_Input), .A(multiplexer_1_out),
    .Answer(Shift_Unit_answer), .Overflow(OverFlow));
  Multiplexer #(.select(2), .width(8)) multiplexer_2 (
    .in0(Arithmetic_Unit_answer), .in1(Logical_Unit_out_4), .in2(Shift_Unit_answer), .in3({8{1'b0}}),
    .out(Answer), .sel(Selection_Bits[1:0]));  // open: en

  // Notes on the sheet:
  //   s4 s3 s2 s1 s0
  //   Selection Description
  //   Selecting Unit
  //   S1   S0  Description
  //   0    0    Arithmetic Unit
  //   0    1    Logic Unit
  //   1    0    Shift Unit
  //   0    0    AND
  //   0    1    OR
  //   1    0    XOR
  //   1    1   NOT
  //   Selecting Logic Operation
  //   S1   S0  Description
  //   Selecting Arithmetic Operation
  //   S3  S2  Cin  Description
  //   ------------------------------------
  //   0  0  0  Add
  //   0  0  1  Add with Carry
  //   0  1  0  Subtract with Carry
  //   0  1  1  Subtract
  //   1  0  0  Transer A
  //   1  0  1  Increment A
  //   1  1  0  Decrement A
  //   1  1  1  Transfer A
  //   Shrey Viradiya
  //   18BCE259
  //   Arithmetic Logic and Shift Unit
  //   Selecting Shift Operation
  //   S4  S3  S2  Description
  //   ------------------------------------
  //   0  0  0  Logical Shift Left
  //   0  0  1  Logical Shift Right
  //   0  1  0  Circular Shift Left
  //   0  1  1 Circular Shift Right
  //   1  0  0  Arithmetic Shift Left
  //   1  0  1  Arithmetic Shift Right
endmodule

// AU
module Arithmetic_Unit (
  input  Cin,
  input  [7:0] A,
  input  [7:0] B,
  input  [1:0] Selection,
  output [7:0] Answer,
  output Cout
);

  wire [7:0] multiplexer_1_out, not_1_out, not_2_out;

  assign not_1_out = ~B;  // NOT_Gate not_1, 8 bits wide
  assign not_2_out = ~{8{1'b0}};  // NOT_Gate not_2, 8 bits wide
  Multiplexer #(.select(2), .width(8)) multiplexer_1 (
    .in0(B), .in1(not_1_out), .in2({8{1'b0}}), .in3(not_2_out), .out(multiplexer_1_out), .sel(Selection));  // open: en
  Adder adder_1 (.a(A), .b(multiplexer_1_out), .out(Answer), .cin(Cin), .cout(Cout));

  // Notes on the sheet:
  //   Arithmetic Unit
endmodule

// LU
module Logical_Unit (
  input  [1:0] Selection,
  input  [7:0] A,
  input  [7:0] B,
  output [7:0] out_4
);

  wire [7:0] And_out, not_1_out, OR_out, XOR_out;

  assign And_out = A & B;  // AND_Gate And, 8 bits wide
  assign OR_out = A | B;  // OR_Gate OR, 8 bits wide
  assign XOR_out = A ^ B;  // XOR_Gate XOR, 8 bits wide
  assign not_1_out = ~A;  // NOT_Gate not_1, 8 bits wide
  Multiplexer #(.select(2), .width(8)) multiplexer_1 (
    .in0(And_out), .in1(OR_out), .in2(XOR_out), .in3(not_1_out), .out(out_4), .sel(Selection));  // open: en

  // Notes on the sheet:
  //   Logical Unit
endmodule

// SU
module Shift_Unit (
  input  [2:0] Selection,
  input  Serial_Input,
  input  [7:0] A,
  output [7:0] Answer,
  output Overflow
);

  Multiplexer #(.select(3)) multiplexer_1 (
    .in0(Serial_Input), .in1(A[1]), .in2(A[7]), .in3(A[1]), .in4(1'b0), .in5(A[1]), .in6(1'b0), .in7(1'b0),
    .out(Answer[0]), .sel(Selection));  // open: en
  Multiplexer #(.select(3)) multiplexer_2 (
    .in0(A[0]), .in1(A[2]), .in2(A[0]), .in3(A[2]), .in4(A[0]), .in5(A[2]), .in6(1'b0), .in7(1'b0),
    .out(Answer[1]), .sel(Selection));  // open: en
  Multiplexer #(.select(3)) multiplexer_3 (
    .in0(A[1]), .in1(A[3]), .in2(A[1]), .in3(A[3]), .in4(A[1]), .in5(A[3]), .in6(1'b0), .in7(1'b0),
    .out(Answer[2]), .sel(Selection));  // open: en
  Multiplexer #(.select(3)) multiplexer_4 (
    .in0(A[2]), .in1(A[4]), .in2(A[2]), .in3(A[4]), .in4(A[2]), .in5(A[4]), .in6(1'b0), .in7(1'b0),
    .out(Answer[3]), .sel(Selection));  // open: en
  Multiplexer #(.select(3)) multiplexer_5 (
    .in0(A[3]), .in1(A[5]), .in2(A[3]), .in3(A[5]), .in4(A[3]), .in5(A[5]), .in6(1'b0), .in7(1'b0),
    .out(Answer[4]), .sel(Selection));  // open: en
  Multiplexer #(.select(3)) multiplexer_6 (
    .in0(A[4]), .in1(A[6]), .in2(A[4]), .in3(A[6]), .in4(A[4]), .in5(A[6]), .in6(1'b0), .in7(1'b0),
    .out(Answer[5]), .sel(Selection));  // open: en
  Multiplexer #(.select(3)) multiplexer_7 (
    .in0(A[5]), .in1(A[7]), .in2(A[5]), .in3(A[7]), .in4(A[5]), .in5(A[7]), .in6(1'b0), .in7(1'b0),
    .out(Answer[6]), .sel(Selection));  // open: en
  Multiplexer #(.select(3)) multiplexer_8 (
    .in0(A[6]), .in1(Serial_Input), .in2(A[6]), .in3(A[0]), .in4(A[6]), .in5(A[7]), .in6(1'b0), .in7(1'b0),
    .out(Answer[7]), .sel(Selection));  // open: en
  xor xor_1 (Overflow, A[6], A[7]);

  // Notes on the sheet:
  //   Serial Input
  //   0
  //   7
  //   0
  //   7
  //   1
  //   2
  //   2
  //   3
  //   4
  //   5
  //   6
  //   0
  //   1
  //   2
  //   3
  //   4
  //   5
  //   6
  //   7
  //   Shift Unit
endmodule
