// Logisim project CA_project_final.circ as structural Verilog: 2 circuits, main circuit Booth's_Algorithm
module Booth_s_Algorithm (
);

  wire AC_out, and_1_out, and_2_out, clock_1_out, counter_1_q, not_1_out, not_3_out, or_1_out, QR_out;
  wire [1:0] Q_n_1_q0;
  wire [3:0] SC_q, xor_1_out;
  wire [7:0] AC_q7, adder_1_out, BR_q7, multiplexer_1_out, not_2_out;

  Shift_Register BR (
    .q0(BR_q7[7]), .q1(BR_q7[6]), .q2(BR_q7[5]), .q3(BR_q7[4]), .q4(BR_q7[3]), .q5(BR_q7[2]), .q6(BR_q7[1]),
    .q7(BR_q7[0]));  // open: shift, in, clk, out, load, clr, d0, d1, d2, d3, d4, d5, d6, d7
  not not_1 (not_1_out, counter_1_q);
  Shift_Register AC (
    .shift(counter_1_q), .in(AC_q7[7]), .clk(and_1_out), .out(AC_out), .load(not_1_out), .d0(adder_1_out[7]),
    .q0(AC_q7[7]), .d1(adder_1_out[6]), .q1(AC_q7[6]), .d2(adder_1_out[5]), .q2(AC_q7[5]),
    .d3(adder_1_out[4]), .q3(AC_q7[4]), .d4(adder_1_out[3]), .q4(AC_q7[3]), .d5(adder_1_out[2]),
    .q5(AC_q7[2]), .d6(adder_1_out[1]), .q6(AC_q7[1]), .d7(adder_1_out[0]), .q7(AC_q7[0]));  // open: clr
  and and_1 (and_1_out, clock_1_out, or_1_out);
  Clock clock_1 (.out(clock_1_out));
  Adder adder_1 (.a(multiplexer_1_out), .b(AC_q7), .out(adder_1_out), .cin(and_2_out));  // open: cout
  Counter #(.width(1), .max('h1)) counter_1 (.Q(counter_1_q), .clk(and_1_out));  // open: load, D, count, carry, clr
  or or_1 (or_1_out, xor_1_out[3], xor_1_out[2], xor_1_out[1], xor_1_out[0]);
  Shift_Register QR (
    .shift(counter_1_q), .in(AC_out), .clk(and_1_out), .out(QR_out), .q7(Q_n_1_q0[1]));  // open: load, clr, d0, q0, d1, q1, d2, q2, d3, q3, d4, q4, d5, q5, d6, q6, d7
  Counter #(.width(4), .max('h8)) SC (
    .D(4'b0001), .count(counter_1_q), .Q(SC_q), .clk(and_1_out));  // open: load, carry, clr
  assign xor_1_out = 4'b1000 ^ SC_q;  // XOR_Gate xor_1, 4 bits wide
  Shift_Register #(.length(1)) Q_n_1 (
    .shift(counter_1_q), .in(QR_out), .clk(and_1_out), .q0(Q_n_1_q0[0]));  // open: out, load, clr, d0
  assign not_2_out = ~BR_q7;  // NOT_Gate not_2, 8 bits wide
  not not_3 (not_3_out, Q_n_1_q0[0]);
  Multiplexer #(.select(2), .width(8)) multiplexer_1 (
    .in0({8{1'b0}}), .in1(BR_q7), .in2(not_2_out), .in3({8{1'b0}}), .out(multiplexer_1_out), .sel(Q_n_1_q0));  // open: en
  and and_2 (and_2_out, not_3_out, Q_n_1_q0[1]);

  // Notes on the sheet:
  //   Alternate Clock Pulse Line
  //   Clock Pulse Line
  //   SC
  //   Stopping System After n SCs
  //   Booths Algorithm
  //   18BCE245
  //   18BCE259
  //   Instructions
  //   1. Make sure to reset the AC
  //   2. Enter the numbers A and B in BR and QR
  //   3. Start simulation i.e. start tick enable from Simulate menu
  //   4. After 8 SC counts answer will be stored in the AC QR
  //   5. After 8 SC counts circuit will stop automatically
endmodule

module Hardware_Algorithm (
  input  Bs,
  input  Qs,
  output As
);

  wire A_out, adder_1_cout, and_1_out, and_2_out, clock_1_out, counter_1_q, E_out, not_1_out, or_1_out;
  wire [3:0] SC_q, xor_1_out;
  wire [7:0] A_q7, adder_1_out, B_q7, Q_q7;

  Shift_Register B (
    .q0(B_q7[7]), .q1(B_q7[6]), .q2(B_q7[5]), .q3(B_q7[4]), .q4(B_q7[3]), .q5(B_q7[2]), .q6(B_q7[1]),
    .q7(B_q7[0]));  // open: shift, in, clk, out, load, clr, d0, d1, d2, d3, d4, d5, d6, d7
  and and_1 (and_1_out, Q_q7[0], not_1_out);
  not not_1 (not_1_out, counter_1_q);
  and and_2 (and_2_out, clock_1_out, or_1_out);
  Clock clock_1 (.out(clock_1_out));
  Shift_Register #(.length(1)) E (
    .shift(counter_1_q), .in(1'b0), .clk(and_2_out), .out(E_out), .load(and_1_out), .d0(adder_1_cout));  // open: clr, q0
  Counter #(.width(1), .max('h1)) counter_1 (.Q(counter_1_q), .clk(and_2_out));  // open: load, D, count, carry, clr
  Shift_Register A (
    .shift(counter_1_q), .in(E_out), .clk(and_2_out), .out(A_out), .load(and_1_out), .d0(adder_1_out[7]),
    .q0(A_q7[7]), .d1(adder_1_out[6]), .q1(A_q7[6]), .d2(adder_1_out[5]), .q2(A_q7[5]), .d3(adder_1_out[4]),
    .q3(A_q7[4]), .d4(adder_1_out[3]), .q4(A_q7[3]), .d5(adder_1_out[2]), .q5(A_q7[2]), .d6(adder_1_out[1]),
    .q6(A_q7[1]), .d7(adder_1_out[0]), .q7(A_q7[0]));  // open: clr
  Adder adder_1 (.a(B_q7), .b(A_q7), .out(adder_1_out), .cout(adder_1_cout));  // open: cin
  Counter #(.width(4), .max('h8)) SC (
    .D(4'b0001), .count(counter_1_q), .Q(SC_q), .clk(and_2_out));  // open: load, carry, clr
  or or_1 (or_1_out, xor_1_out[3], xor_1_out[2], xor_1_out[1], xor_1_out[0]);
  assign xor_1_out = 4'b1000 ^ SC_q;  // XOR_Gate xor_1, 4 bits wide
  Shift_Register Q (
    .shift(counter_1_q), .in(A_out), .clk(and_2_out), .q0(Q_q7[7]), .q1(Q_q7[6]), .q2(Q_q7[5]), .q3(Q_q7[4]),
    .q4(Q_q7[3]), .q5(Q_q7[2]), .q6(Q_q7[1]), .q7(Q_q7[0]));  // open: out, load, clr, d0, d1, d2, d3, d4, d5, d6, d7
  xor xor_2 (As, Bs, Qs);

  // Notes on the sheet:
  //   Alternate Clock Pulse
  //   Instructions
  //   clock
  //   Stopping System After n SCs
  //   1. Reset the circuit, make sure A is 0
  //   2. load P nd Q in B and Q for multipliication P*Q
  //   3. load sign bits of P and Q in Bs and Qs
  //   4. start simulation by tick enabling in Simulate menu
  //   5. After 8 SC circuit will stop automatically answer will be in AQ
  //   Hardware Algorithm
  //   18BCE245
  //   18BCE259
endmodule
