// Logisim project BoothsAlgo.circ as structural Verilog: 1 circuit, main circuit main
module main (
);

  wire and_1_out, and_2_out, AR_out, clock_1_out, counter_1_q, not_1_out, not_3_out, or_1_out, QR_out;
  wire [1:0] Q_n_1_q0;
  wire [2:0] SC_q, xor_1_out;
  wire [5:0] adder_1_out, AR_q5, BR_q5, multiplexer_1_out, not_2_out;

  Shift_Register #(.length(6)) BR (
    .q0(BR_q5[5]), .q1(BR_q5[4]), .q2(BR_q5[3]), .q3(BR_q5[2]), .q4(BR_q5[1]), .q5(BR_q5[0]));  // open: shift, in, clk, out, load, clr, d0, d1, d2, d3, d4, d5
  not not_1 (not_1_out, counter_1_q);
  Shift_Register #(.length(6)) AR (
    .shift(counter_1_q), .in(AR_q5[5]), .clk(and_1_out), .out(AR_out), .load(not_1_out), .d0(adder_1_out[5]),
    .q0(AR_q5[5]), .d1(adder_1_out[4]), .q1(AR_q5[4]), .d2(adder_1_out[3]), .q2(AR_q5[3]),
    .d3(adder_1_out[2]), .q3(AR_q5[2]), .d4(adder_1_out[1]), .q4(AR_q5[1]), .d5(adder_1_out[0]), .q5(AR_q5[0]));  // open: clr
  and and_1 (and_1_out, clock_1_out, or_1_out);
  Clock clock_1 (.out(clock_1_out));
  Adder #(.width(6)) adder_1 (.a(AR_q5), .b(multiplexer_1_out), .out(adder_1_out), .cin(and_2_out));  // open: cout
  Counter #(.width(1), .max('h1)) counter_1 (.Q(counter_1_q), .clk(and_1_out));  // open: load, D, count, carry, clr
  or or_1 (or_1_out, xor_1_out[2], xor_1_out[1], xor_1_out[0]);
  assign xor_1_out = 3'b110 ^ SC_q;  // XOR_Gate xor_1, 3 bits wide
  Shift_Register #(.length(6)) QR (
    .shift(counter_1_q), .in(AR_out), .clk(and_1_out), .out(QR_out), .q5(Q_n_1_q0[1]));  // open: load, clr, d0, q0, d1, q1, d2, q2, d3, q3, d4, q4, d5
  Counter #(.width(3), .max('h6)) SC (
    .D(3'b001), .count(counter_1_q), .Q(SC_q), .clk(and_1_out));  // open: load, carry, clr
  Shift_Register #(.length(1)) Q_n_1 (
    .shift(counter_1_q), .in(QR_out), .clk(and_1_out), .q0(Q_n_1_q0[0]));  // open: out, load, clr, d0
  Multiplexer #(.select(2), .width(6)) multiplexer_1 (
    .in0({6{1'b0}}), .in1(BR_q5), .in2(not_2_out), .in3({6{1'b0}}), .out(multiplexer_1_out), .sel(Q_n_1_q0));  // open: en
  assign not_2_out = ~BR_q5;  // NOT_Gate not_2, 6 bits wide
  not not_3 (not_3_out, Q_n_1_q0[0]);
  and and_2 (and_2_out, not_3_out, Q_n_1_q0[1]);
endmodule
